# Fritzing sketch proj10 (saved by Fritzing 0.9.3b)
breadboards: 1

parts:
  Componente1 = Arduino Uno (Rev3)
  LED1 = smd LED [color="Red (633nm)" package="0603 [SMD]"]
  R1 = Resistor [tolerance=±5% resistance=220 package="0402 [SMD]"]
  R2 = Resistor [tolerance=±5% resistance=220 package="0402 [SMD]"]
  R3 = Photocell (LDR) [package=THT]

nets:
  N1: Componente1.A0, R1.Pin_0, R3.pin_1
  N2: Componente1.D11_PWM/MOSI, R2.Pin_1
  N3: Componente1.GND, LED1.cathode, R1.Pin_1
  N4: Componente1.5V, R3.pin_0
  N5: LED1.anode, R2.Pin_0
