# Fritzing sketch proj15 (saved by Fritzing 0.9.3b)
breadboards: 1

parts:
  Componente1 = Arduino Uno (Rev3)
  LED1 = smd LED [color="Blue (430nm)" package="0603 [SMD]"]
  LED2 = smd LED [color="Infrared (850nm)" package="0603 [SMD]"]
  R1 = Resistor [tolerance=±5% resistance=5k package="0402 [SMD]"]
  R2 = Resistor [tolerance=±5% resistance=220 package="0402 [SMD]"]

nets:
  N1: Componente1.A0, LED1.anode, R1.Pin_0
  N2: Componente1.GND, LED1.cathode, LED2.cathode
  N3: Componente1.5V, R1.Pin_1, R2.Pin_1
  N4: LED2.anode, R2.Pin_0
