# Fritzing sketch proj16 (saved by Fritzing 0.9.3b)
breadboards: 1

parts:
  Componente1 = Arduino Uno (Rev3)
  LED1 = smd LED [color="Blue (430nm)" package="0603 [SMD]"]
  R1 = Resistor [tolerance=±5% resistance=220 package="0603 [SMD]"]

nets:
  N1: Componente1.D12/MISO, R1.Pin_1
  N2: Componente1.GND, LED1.cathode
  N3: LED1.anode, R1.Pin_0
