# Fritzing sketch proj18 (saved by Fritzing 0.9.3b)
breadboards: 1

parts:
  R1 = Resistor [tolerance=±5% resistance=220 package=THT]
  R2 = Resistor [tolerance=±5% resistance=220 package=THT]
  R3 = Resistor [tolerance=±5% resistance=220 package=THT]
  LED1 = smd LED [color="Red (633nm)" package="1206 [SMD]"]
  LED2 = smd LED [color="Red (633nm)" package="1206 [SMD]"]
  LED3 = smd LED [color="Red (633nm)" package="1206 [SMD]"]
  R4 = Rotary Potentiometer (Small) [maximum_resistance=100kΩ package=THT]
  Componente1 = Arduino Uno (Rev3)

nets:
  N1: R1.Pin_0, LED1.anode
  N2: R1.Pin_1, Componente1.D11_PWM/MOSI
  N3: R2.Pin_0, LED3.anode
  N4: R2.Pin_1, Componente1.D10_PWM/SS
  N5: R3.Pin_0, LED2.anode
  N6: R3.Pin_1, Componente1.D9_PWM
  N7: LED1.cathode, LED2.cathode, LED3.cathode, R4.leg1, Componente1.GND
  N8: R4.wiper, Componente1.A0
  N9: R4.leg2, Componente1.5V
