# Fritzing sketch proj3 (saved by Fritzing 0.9.3b)
breadboards: 1

parts:
  Componente1 = Arduino Uno (Rev3)
  S1 = SWITCH-MOMENTARY-2 [package=tactile-pth-12mm]
  R1 = Resistor [tolerance=±5% resistance=220 package=THT]
  R2 = Resistor [tolerance=±5% resistance=220 package=THT]
  LED1 = smd LED [color="Red (633nm)" package="0603 [SMD]"]

nets:
  N1: Componente1.D8, R1.Pin_0
  N2: Componente1.GND, S1.1
  N3: Componente1.D7, R2.Pin_1
  N4: Componente1.5V, R1.Pin_1, LED1.cathode
  N5: R2.Pin_0, LED1.anode
