# Fritzing sketch proj4 (saved by Fritzing 0.9.3b)
breadboards: 1

parts:
  R1 = Resistor [tolerance=±5% resistance=220 package=THT]
  LED1 = smd LED [color="Red (633nm)" package="0603 [SMD]"]
  S1 = Tilt Switch [package=THT]
  Componente1 = Arduino Uno (Rev3)

nets:
  N1: R1.Pin_0, LED1.anode
  N2: R1.Pin_1, Componente1.D11_PWM/MOSI
  N3: LED1.cathode, S1.Pin_2, Componente1.GND
  N4: S1.Pin_1, Componente1.D2
