# Fritzing sketch proj5 (saved by Fritzing 0.9.3b)
breadboards: 1

parts:
  Componente1 = Arduino Uno (Rev3)
  J1 = Piezo Speaker
  R1 = Resistor [tolerance=±5% resistance=220 package="0402 [SMD]"]

nets:
  N1: Componente1.GND, J1.pin1
  N2: Componente1.D4, R1.Pin_1
  N3: J1.pin2, R1.Pin_0
