# Fritzing sketch proj6 (saved by Fritzing 0.9.3b)
breadboards: 1

parts:
  Componente1 = Arduino Uno (Rev3)
  R1 = Resistor [tolerance=±5% resistance=220 package="0603 [SMD]"]
  LED1 = RGB LED (com. cathode, rgb) [package="5 mm [THT]"]
  R2 = Resistor [tolerance=±5% resistance=220 package="0603 [SMD]"]
  R3 = Resistor [tolerance=±5% resistance=220 package="0603 [SMD]"]

nets:
  N1: Componente1.GND, LED1.common_cathode
  N2: Componente1.D3_PWM, R2.Pin_1
  N3: Componente1.D5_PWM, R1.Pin_1
  N4: Componente1.D6_PWM, R3.Pin_0
  N5: R1.Pin_0, LED1.green_anode
  N6: LED1.red_anode, R3.Pin_1
  N7: LED1.blue_anode, R2.Pin_0
