# Fritzing sketch proj9 (saved by Fritzing 0.9.3b)
breadboards: 1

parts:
  R1 = Resistor [tolerance=±5% resistance=220 package=THT]
  LED1 = smd LED [color="Red (633nm)" package="1206 [SMD]"]
  R4 = Rotary Potentiometer (Small) [maximum_resistance=100kΩ package=THT]
  Componente1 = Arduino Uno (Rev3)

nets:
  N1: R1.Pin_0, LED1.anode
  N2: R1.Pin_1, Componente1.D11_PWM/MOSI
  N3: LED1.cathode, R4.leg1, Componente1.GND
  N4: R4.wiper, Componente1.A0
  N5: R4.leg2, Componente1.5V
